// Logisim project ex5.circ as structural Verilog: 1 circuit, main circuit Running_LED
module Running_LED (
  input  [7:0] INITIAL_LED,
  input  RST,
  output [7:0] OUT_LED
);

  wire clock_1_out;
  wire [7:0] multiplexer_1_out, register_1_q;

  Clock clock_1 (.out(clock_1_out));
  LED led_1 (.in(OUT_LED[7]));
  Multiplexer #(.width(8)) multiplexer_1 (.in0(OUT_LED), .in1(INITIAL_LED), .out(multiplexer_1_out), .sel(RST));
  LED led_2 (.in(OUT_LED[6]));
  Register register_1 (.D(multiplexer_1_out), .clk(clock_1_out), .Q(register_1_q));  // open: en, clr
  LED led_3 (.in(OUT_LED[5]));
  Shifter #(.shift("rr")) shifter_1 (.in(register_1_q), .\dist (3'b001), .out(OUT_LED));
  LED led_4 (.in(OUT_LED[4]));
  LED led_5 (.in(OUT_LED[3]));
  LED led_6 (.in(OUT_LED[2]));
  LED led_7 (.in(OUT_LED[1]));
  LED led_8 (.in(OUT_LED[0]));

  // Notes on the sheet:
  //   PUT CIRCUITS HERE
endmodule
