// Logisim project ex5_revised.circ as structural Verilog: 1 circuit, main circuit main
module main (
  input  [7:0] INITIAL_LED,
  input  RST,
  output [7:0] OUT_LED
);

  wire clk, comparator_1_gt;
  wire [7:0] cnt, multiplexer_1_out, register_1_q, shifter_1_out;

  Clock clock_1 (.out(clk));
  LED led_1 (.in(OUT_LED[7]));
  Counter #(.ongoal("stay")) counter_1 (.clr(RST), .up(1'b1), .clk(clk), .Q(cnt));  // open: load, count, D, carry
  Multiplexer #(.width(8)) multiplexer_1 (.in0(OUT_LED), .in1(INITIAL_LED), .out(multiplexer_1_out), .sel(RST));
  LED led_2 (.in(OUT_LED[6]));
  Register register_1 (.D(multiplexer_1_out), .clk(clk), .Q(register_1_q));  // open: en, clr
  LED led_3 (.in(OUT_LED[5]));
  Shifter #(.shift("rr")) shifter_1 (.in(register_1_q), .\dist (3'b001), .out(shifter_1_out));
  Comparator comparator_1 (.a(cnt), .b(8'h8), .gt(comparator_1_gt));  // open: eq, lt
  LED led_4 (.in(OUT_LED[4]));
  Multiplexer #(.width(8)) multiplexer_2 (
    .in0(shifter_1_out), .in1(register_1_q), .out(OUT_LED), .sel(comparator_1_gt));
  LED led_5 (.in(OUT_LED[3]));
  LED led_6 (.in(OUT_LED[2]));
  LED led_7 (.in(OUT_LED[1]));
  LED led_8 (.in(OUT_LED[0]));

  // Notes on the sheet:
  //   PUT CIRCUITS HERE
endmodule
