// Logisim project ex3.circ as structural Verilog: 1 circuit, main circuit Split
module Split (
  input  [7:0] IN1,
  output OUT1,
  output OUT2,
  output [8:0] OUT3,
  output [8:0] OUT4
);

  wire comparator_1_gt;
  wire [3:0] bitadder_1_out;
  wire [7:0] neg;

  not not_1 (OUT3[8], OUT1);
  xor xor_1 (OUT1, IN1[0], IN1[1], IN1[2], IN1[3], IN1[4], IN1[5], IN1[6], IN1[7]);
  Comparator #(.mode("unsigned"), .width(1)) comparator_1 (.a(OUT2), .b(1'b0), .gt(comparator_1_gt));  // open: eq, lt
  Negator negator_1 (.in(IN1), .out(neg));
  BitAdder bitadder_1 (.in0(IN1), .out(bitadder_1_out));
  Multiplexer #(.width(9)) multiplexer_1 (.in0({OUT2, IN1}), .in1({OUT2, neg}), .out(OUT4), .sel(comparator_1_gt));
  Comparator #(.mode("unsigned"), .width(4)) comparator_2 (.a(bitadder_1_out), .b(4'b0100), .gt(OUT2));  // open: eq, lt

  assign OUT3[7:0] = IN1;

  // Other names for the same wires on the sheet: neg[8] = OUT2; pos[8:0] = {OUT2, IN1}; IN1_0 = IN1[0];
  //   IN1_1 = IN1[1]; IN1_2 = IN1[2]; IN1_3 = IN1[3]; IN1_4 = IN1[4]; IN1_5 = IN1[5]; IN1_6 = IN1[6]; IN1_7 = IN1[7]

  // Notes on the sheet:
  //   PUT CIRCUITRY HERE
endmodule
