// Logisim project ex2.circ as structural Verilog: 1 circuit, main circuit main
module main (
  input  clk,
  input  rst,
  input  pc_update,
  input  [31:0] new_addr,
  output [31:0] current_addr
);
endmodule
