// Logisim project ex2.circ as structural Verilog: 1 circuit, main circuit main
module main (
  input  clk,
  input  rst,
  input  pc_update,
  input  [31:0] new_addr,
  output [31:0] current_addr
);

  wire [31:0] adder_1_out, multiplexer_1_out, new_addr_aligned, shifter_1_out;

  Multiplexer #(.width(32)) multiplexer_1 (
    .in0(adder_1_out), .in1(new_addr_aligned), .out(multiplexer_1_out), .sel(pc_update));
  Register #(.width(32)) PC (.D(multiplexer_1_out), .clk(clk), .Q(current_addr), .clr(rst));  // open: en
  Shifter #(.shift("lr"), .width(32)) shifter_1 (.in(new_addr), .\dist (5'b00010), .out(shifter_1_out));
  Adder #(.width(32)) adder_1 (.a(current_addr), .b(32'h4), .out(adder_1_out));  // open: cin, cout
  Shifter #(.width(32)) shifter_2 (.in(shifter_1_out), .\dist (5'b00010), .out(new_addr_aligned));
endmodule
