// Logisim project ex2_test.circ as structural Verilog: 1 circuit, main circuit test
module test (
  output [3:0] count,
  output halt,
  output out_3,
  output out_4,
  output [31:0] out_5,
  output [31:0] out_addr
);

  wire clk, or_1_out, undriven;
  wire [3:0] adder_1_out;

  Clock clock_1 (.out(clk));
  Register #(.width(4)) register_1 (.D(adder_1_out), .clk(clk), .Q(count), .clr(undriven));  // open: en
  or or_1 (or_1_out, count[0], count[1], count[2], count[3]);
  ROM #(.addrWidth(4), .dataWidth(33)) rom_1 (.addr(count), .data({out_4, out_5}));
  Adder #(.width(4)) adder_1 (.a(4'b0001), .b(count), .out(adder_1_out));  // open: cin, cout
  not not_1 (out_3, or_1_out);
  Comparator #(.width(4)) comparator_1 (.a(count), .b(4'b1111), .eq(halt));  // open: gt, lt
  // Probe on out_5
  // Probe on out_5
  ex2_main main_1 (.clk(clk), .rst(out_3), .pc_update(out_4), .new_addr(out_5), .current_addr(out_addr));

  // Other names for the same wires on the sheet: new_addr[31:0] = out_5; pc_update = out_4; rst = out_3;
  //   Test[3:0] = count

  // Notes on the sheet:
  //   contents of rom_1 (hex, n*v repeats v):
  //   100000000 100000000 0 ade fee34df ade 1aabb1100 80 0 aabbccdd 10f0f0f0f 0 10101010
endmodule
