// Logisim project Lab8.circ as structural Verilog: 4 circuits, main circuit main
module main (
  output [7:0] non_pipe_out,
  output [7:0] pipe_out
);

  wire CLK_out, undriven, undriven_2;
  wire [7:0] Address_Counter_q, rom_1_data;

  Counter Address_Counter (.clk(CLK_out), .Q(Address_Counter_q));  // open: clr, load, up, count, D, carry
  Clock CLK (.out(CLK_out));
  ROM rom_1 (.addr(Address_Counter_q), .data(rom_1_data));
  // Probe on undriven_2
  // Probe on undriven
  non_pipelined non_pipelined_1 (
    .multiplicand(rom_1_data[3:0]), .multiplier(rom_1_data[7:4]), .CLK(CLK_out), .product(non_pipe_out));
  pipelined pipelined_1 (
    .multiplicand(rom_1_data[3:0]), .multiplier(rom_1_data[7:4]), .CLK(CLK_out), .product(pipe_out));

  // Notes on the sheet:
  //   contents of rom_1 (hex, n*v repeats v):
  //   13 a2 fc 8f 1c 2 b0
endmodule

module non_pipelined (
  input  [3:0] multiplicand,
  input  [3:0] multiplier,
  input  CLK,
  output [7:0] product
);

  wire [7:0] shift_and_add_1_partial_product, shift_and_add_1_shifted_multiplicand,
       shift_and_add_2_partial_product, shift_and_add_2_shifted_multiplicand,
       shift_and_add_3_partial_product, shift_and_add_3_shifted_multiplicand, shift_and_add_4_partial_product;

  shift_and_add shift_and_add_1 (
    .current_sum({8{1'b0}}), .multiplicand({4'b0000, multiplicand}), .multiplier(multiplier[0]),
    .partial_product(shift_and_add_1_partial_product),
    .shifted_multiplicand(shift_and_add_1_shifted_multiplicand));
  shift_and_add shift_and_add_2 (
    .current_sum(shift_and_add_1_partial_product), .multiplicand(shift_and_add_1_shifted_multiplicand),
    .multiplier(multiplier[1]), .partial_product(shift_and_add_2_partial_product),
    .shifted_multiplicand(shift_and_add_2_shifted_multiplicand));
  shift_and_add shift_and_add_3 (
    .current_sum(shift_and_add_2_partial_product), .multiplicand(shift_and_add_2_shifted_multiplicand),
    .multiplier(multiplier[2]), .partial_product(shift_and_add_3_partial_product),
    .shifted_multiplicand(shift_and_add_3_shifted_multiplicand));
  shift_and_add shift_and_add_4 (
    .current_sum(shift_and_add_3_partial_product), .multiplicand(shift_and_add_3_shifted_multiplicand),
    .multiplier(multiplier[3]), .partial_product(shift_and_add_4_partial_product));  // open: shifted_multiplicand
  Register register_1 (.D(shift_and_add_4_partial_product), .clk(CLK), .Q(product));  // open: en, clr
endmodule

module pipelined (
  input  [3:0] multiplicand,
  input  [3:0] multiplier,
  input  CLK,
  output [7:0] product
);

  wire register_3_q, register_4_q;
  wire [7:0] register_1_q, register_2_q, shift_and_add_1_partial_product,
       shift_and_add_1_shifted_multiplicand, shift_and_add_2_partial_product,
       shift_and_add_2_shifted_multiplicand, shift_and_add_3_partial_product,
       shift_and_add_3_shifted_multiplicand, shift_and_add_4_partial_product;

  shift_and_add shift_and_add_1 (
    .current_sum({8{1'b0}}), .multiplicand({4'b0000, multiplicand}), .multiplier(multiplier[0]),
    .partial_product(shift_and_add_1_partial_product),
    .shifted_multiplicand(shift_and_add_1_shifted_multiplicand));
  shift_and_add shift_and_add_2 (
    .current_sum(shift_and_add_1_partial_product), .multiplicand(shift_and_add_1_shifted_multiplicand),
    .multiplier(multiplier[1]), .partial_product(shift_and_add_2_partial_product),
    .shifted_multiplicand(shift_and_add_2_shifted_multiplicand));
  Register register_1 (.D(shift_and_add_2_partial_product), .clk(CLK), .Q(register_1_q));  // open: en, clr
  Register register_2 (.D(shift_and_add_2_shifted_multiplicand), .clk(CLK), .Q(register_2_q));  // open: en, clr
  Register #(.width(1)) register_3 (.D(multiplier[2]), .clk(CLK), .Q(register_3_q));  // open: en, clr
  Register #(.width(1)) register_4 (.D(multiplier[3]), .clk(CLK), .Q(register_4_q));  // open: en, clr
  shift_and_add shift_and_add_3 (
    .current_sum(register_1_q), .multiplicand(register_2_q), .multiplier(register_3_q),
    .partial_product(shift_and_add_3_partial_product),
    .shifted_multiplicand(shift_and_add_3_shifted_multiplicand));
  shift_and_add shift_and_add_4 (
    .current_sum(shift_and_add_3_partial_product), .multiplicand(shift_and_add_3_shifted_multiplicand),
    .multiplier(register_4_q), .partial_product(shift_and_add_4_partial_product));  // open: shifted_multiplicand
  Register register_5 (.D(shift_and_add_4_partial_product), .clk(CLK), .Q(product));  // open: en, clr

  // Other names for the same wires on the sheet: A[3:0] = multiplicand; ans[7:0] = product
endmodule

module shift_and_add (
  input  [7:0] current_sum,
  input  [7:0] multiplicand,
  input  multiplier,
  output [7:0] partial_product,
  output [7:0] shifted_multiplicand
);

  wire [7:0] multiplexer_1_out;

  Multiplexer #(.enable("true"), .width(8)) multiplexer_1 (
    .in0({8{1'b0}}), .in1(multiplicand), .out(multiplexer_1_out), .sel(multiplier));  // open: en
  Adder adder_1 (.a(current_sum), .b(multiplexer_1_out), .out(partial_product));  // open: cin, cout
  Shifter shifter_1 (.in(multiplicand), .\dist (3'b001), .out(shifted_multiplicand));
endmodule
