// Logisim project Q1.circ as structural Verilog: 2 circuits, main circuit main
module main (
  input  in_1,
  input  in_2,
  output out_3,
  output out_4,
  output out_5
);

  wire nand_1_out;

  nand nand_1 (nand_1_out, in_1, in_2);
  and and_1 (out_3, in_1, nand_1_out);
  and and_2 (out_5, nand_1_out, in_2);
  nor nor_1 (out_4, out_3, out_5);
endmodule

module TwoBit (
  input  A1,
  input  A0,
  input  B1,
  input  B0,
  output Y0,
  output Y1,
  output Y2
);

  wire and_1_out, and_2_out, HighBig, HighEqual, HighSmall, LowBig, LowEqual, LowSmall;

  Comparator #(.mode("unsigned"), .width(1)) comparator_1 (
    .a(A1), .b(B1), .gt(HighBig), .eq(HighEqual), .lt(HighSmall));
  Comparator #(.mode("unsigned"), .width(1)) comparator_2 (.a(A0), .b(B0), .gt(LowBig), .eq(LowEqual), .lt(LowSmall));
  and and_1 (and_1_out, HighEqual, LowBig);
  and and_2 (and_2_out, HighEqual, LowSmall);
  or or_1 (Y0, HighBig, and_1_out);
  and and_3 (Y1, HighEqual, LowEqual);
  or or_2 (Y2, HighSmall, and_2_out);
endmodule
