// Logisim project Q3.circ as structural Verilog: 1 circuit, main circuit main
module main (
  input  in_put,
  output out_put
);

  wire and_1_out, and_2_out, and_3_out, and_4_out, and_5_out, and_6_out, and_7_out, and_8_out, clk, CS0, CS1,
       CS2, not_1_out, not_2_out, not_3_out, not_4_out, not_5_out, not_6_out, or_1_out, or_2_out, or_3_out;

  Clock clock_1 (.out(clk));
  not not_1 (not_1_out, CS2);
  not not_2 (not_2_out, CS1);
  not not_3 (not_3_out, CS0);
  not not_4 (not_4_out, in_put);
  and and_1 (and_1_out, not_3_out, not_4_out);
  and and_2 (and_2_out, CS2, CS0);
  and and_3 (and_3_out, not_2_out, and_1_out);
  and and_4 (and_4_out, not_2_out, not_3_out);
  and and_5 (and_5_out, not_1_out, and_3_out);
  or or_1 (or_1_out, CS2, and_4_out);
  not not_5 (not_5_out, CS1);
  not not_6 (not_6_out, CS0);
  Register #(.width(1)) NS2 (.D(1'b1), .clk(clk), .Q(CS2));  // open: en, clr
  Register #(.width(1)) NS1 (.D(or_2_out), .clk(clk), .Q(CS1));  // open: en, clr
  or or_2 (or_2_out, and_2_out, and_5_out);
  Register #(.width(1)) NS0 (.D(and_6_out), .clk(clk), .Q(CS0));  // open: en, clr
  and and_6 (and_6_out, or_1_out, in_put);
  and and_7 (and_7_out, not_5_out, not_6_out);
  or or_3 (or_3_out, and_7_out, and_8_out);
  and and_8 (and_8_out, CS1, CS0);
  and and_9 (out_put, CS2, or_3_out);
endmodule
